// Logisim project somador_display.circ as structural Verilog: 5 circuits, main circuit main
module main (
  input  in_1,
  input  in_2,
  input  in_3,
  input  in_4,
  input  in_5,
  input  in_6,
  input  in_7,
  input  in_8,
  input  in_9,
  output out_10,
  output out_11,
  output out_12,
  output out_13,
  output out_14
);

  soma4bits soma4bits_1 (
    .in_2(in_1), .in_3(in_2), .in_4(in_4), .in_5(in_5), .in_6(in_6), .in_7(in_7), .in_8(in_8), .in_9(in_9),
    .in_1(in_3), .out_14(out_13), .out_10(out_10), .out_11(out_11), .out_12(out_12), .out_13(out_14));
endmodule

module meiasoma (
  input  x0,
  input  x1,
  output s0,
  output co0
);

  and and_1 (co0, x1, x0);
  xor xor_1 (s0, x0, x1);
endmodule

module somacompleta (
  input  in_1,
  input  in_2,
  input  in_3,
  output out_4,
  output out_5
);

  wire meiasoma_1_co0, meiasoma_1_s0, meiasoma_2_co0;

  meiasoma meiasoma_1 (.x0(in_2), .x1(in_3), .co0(meiasoma_1_co0), .s0(meiasoma_1_s0));
  meiasoma meiasoma_2 (.x0(in_1), .x1(meiasoma_1_s0), .co0(meiasoma_2_co0), .s0(out_4));
  or or_1 (out_5, meiasoma_1_co0, meiasoma_2_co0);
endmodule

module soma4bits (
  input  in_1,
  input  in_2,
  input  in_3,
  input  in_4,
  input  in_5,
  input  in_6,
  input  in_7,
  input  in_8,
  input  in_9,
  output out_10,
  output out_11,
  output out_12,
  output out_13,
  output out_14
);

  wire somacompleta_1_out_5, somacompleta_2_out_5, somacompleta_3_out_5;

  somacompleta somacompleta_1 (.in_2(in_2), .in_3(in_3), .in_1(in_1), .out_5(somacompleta_1_out_5), .out_4(out_10));
  somacompleta somacompleta_2 (
    .in_2(in_4), .in_3(in_5), .in_1(somacompleta_1_out_5), .out_5(somacompleta_2_out_5), .out_4(out_11));
  somacompleta somacompleta_3 (
    .in_2(in_6), .in_3(in_7), .in_1(somacompleta_2_out_5), .out_5(somacompleta_3_out_5), .out_4(out_12));
  somacompleta somacompleta_4 (.in_2(in_8), .in_3(in_9), .in_1(somacompleta_3_out_5), .out_5(out_14), .out_4(out_13));
endmodule

module decodificador (
  input  e3,
  input  e2,
  input  e1,
  input  e0,
  output a,
  output b,
  output c,
  output d,
  output e,
  output f,
  output g
);
endmodule
