// Logisim project tp0101A_meiosomador.circ as structural Verilog: 2 circuits, main circuit main
module main (
  input  A,
  input  B,
  output R,
  output C
);

  meiosomador meiosomador_1 (.A(A), .B(B), .C___A___B(C), .S___A_xor_B(R));
endmodule

module meiosomador (
  input  A,
  input  B,
  output S___A_xor_B,
  output C___A___B
);

  xor xor_1 (S___A_xor_B, A, B);
  and and_1 (C___A___B, A, B);
endmodule
