// Logisim project tp0102_somadorcompleto.circ as structural Verilog: 3 circuits, main circuit main
module main (
  input  in_1,
  input  in_2,
  input  in_3,
  output out_4,
  output out_5
);

  somador_completo somador_completo_1 (.Ci(in_1), .A(in_2), .B(in_3), .out_4(out_4), .out_5(out_5));
endmodule

module meiosomador (
  input  A,
  input  B,
  output S___A_xor_B,
  output C___A___B
);

  xor xor_1 (S___A_xor_B, A, B);
  and and_1 (C___A___B, A, B);
endmodule

module somador_completo (
  input  Ci,
  input  A,
  input  B,
  output out_4,
  output out_5
);

  wire meiosomador_1_c___a___b, meiosomador_2_c___a___b, meiosomador_2_s___a_xor_b;

  meiosomador meiosomador_1 (
    .A(Ci), .B(meiosomador_2_s___a_xor_b), .C___A___B(meiosomador_1_c___a___b), .S___A_xor_B(out_4));
  meiosomador meiosomador_2 (
    .A(A), .B(B), .C___A___B(meiosomador_2_c___a___b), .S___A_xor_B(meiosomador_2_s___a_xor_b));
  or or_1 (out_5, meiosomador_1_c___a___b, meiosomador_2_c___a___b);
endmodule
