// Logisim project tp0103_somador4bit.circ as structural Verilog: 4 circuits, main circuit main
module main (
  input  in_1,
  input  in_2,
  input  in_3,
  input  in_4,
  input  in_5,
  input  in_6,
  input  in_7,
  input  in_8,
  input  in_9,
  output out_10,
  output out_11,
  output out_12,
  output out_13,
  output out_14
);

  somador4bit somador4bit_1 (
    .in_2(in_2), .in_3(in_3), .in_4(in_4), .in_5(in_5), .in_6(in_6), .in_7(in_7), .in_8(in_8), .in_9(in_9),
    .in_1(in_1), .out_14(out_14), .out_10(out_10), .out_11(out_11), .out_12(out_12), .out_13(out_13));
endmodule

module meiosomador (
  input  A,
  input  B,
  output S___A_xor_B,
  output C___A___B
);

  xor xor_1 (S___A_xor_B, A, B);
  and and_1 (C___A___B, A, B);
endmodule

module somador_completo (
  input  Ci,
  input  A,
  input  B,
  output out_4,
  output out_5
);

  wire meiosomador_1_c___a___b, meiosomador_2_c___a___b, meiosomador_2_s___a_xor_b;

  meiosomador meiosomador_1 (
    .A(Ci), .B(meiosomador_2_s___a_xor_b), .C___A___B(meiosomador_1_c___a___b), .S___A_xor_B(out_4));
  meiosomador meiosomador_2 (
    .A(A), .B(B), .C___A___B(meiosomador_2_c___a___b), .S___A_xor_B(meiosomador_2_s___a_xor_b));
  or or_1 (out_5, meiosomador_1_c___a___b, meiosomador_2_c___a___b);
endmodule

module somador4bit (
  input  in_1,
  input  in_2,
  input  in_3,
  input  in_4,
  input  in_5,
  input  in_6,
  input  in_7,
  input  in_8,
  input  in_9,
  output out_10,
  output out_11,
  output out_12,
  output out_13,
  output out_14
);

  wire somador_completo_1_out_5, somador_completo_2_out_5, somador_completo_3_out_5;

  somador_completo somador_completo_1 (.A(in_2), .B(in_3), .Ci(in_1), .out_5(somador_completo_1_out_5), .out_4(out_10));
  somador_completo somador_completo_2 (
    .A(in_4), .B(in_5), .Ci(somador_completo_1_out_5), .out_5(somador_completo_2_out_5), .out_4(out_11));
  somador_completo somador_completo_3 (
    .A(in_6), .B(in_7), .Ci(somador_completo_2_out_5), .out_5(somador_completo_3_out_5), .out_4(out_12));
  somador_completo somador_completo_4 (
    .A(in_8), .B(in_9), .Ci(somador_completo_3_out_5), .out_5(out_14), .out_4(out_13));
endmodule
